// Logisim project Monocycle-processor.circ as structural Verilog: 8 circuits, main circuit main
// ALU
module main (
);

  wire alu_1_zero, ALUSrc, and_1_out, Branch, CLK, control_1_regwrite, MemToReg, MemWrite, not_1_out, RegDist;
  wire [1:0] ALUOp;
  wire [2:0] alucontrol_1_select;
  wire [4:0] multiplexer_1_out;
  wire [31:0] adder_1_out, adder_2_out, Address_Memory_out_2, alu_1_o, Data_Memory_readed_data,
       multiplexer_2_out, multiplexer_3_out, pc_1_next_address, registers_1_read_data_1,
       registers_1_read_data_2, shifter_1_out, SignExtend, WriteData;

  PC pc_1 (.Address_Input(multiplexer_3_out), .CLK(CLK), .Next_Address(pc_1_next_address));
  Clock clock_1 (.out(CLK));
  Adder #(.width(32)) adder_1 (.a(pc_1_next_address), .b(32'h4), .out(adder_1_out));  // open: cin, cout
  // Probe on Address_Memory_out_2
  Address_Memory Address_Memory (.Instruction_Address(pc_1_next_address), .out_2(Address_Memory_out_2));
  Control control_1 (
    .Instruction(Address_Memory_out_2[31:26]), .RegDst(RegDist), .Branch(Branch), .MemToReg(MemToReg),
    .ALUOp(ALUOp), .MemWrite(MemWrite), .ALUSrc(ALUSrc), .RegWrite(control_1_regwrite));
  Multiplexer #(.width(5), .enable("false")) multiplexer_1 (
    .in0(Address_Memory_out_2[20:16]), .in1(Address_Memory_out_2[15:11]), .out(multiplexer_1_out),
    .sel(RegDist));
  assign SignExtend = {{16{Address_Memory_out_2[15]}}, Address_Memory_out_2[15:0]};  // Bit_Extender bit_extender_1
  Registers registers_1 (
    .Read_Register_1(Address_Memory_out_2[25:21]), .Read_Register_2(Address_Memory_out_2[20:16]),
    .Write_Register(multiplexer_1_out), .Write_Data(WriteData), .Write_Enable(control_1_regwrite), .CLK(CLK),
    .Read_Data_1(registers_1_read_data_1), .Read_data_2(registers_1_read_data_2));
  Multiplexer #(.width(32), .enable("false")) multiplexer_2 (
    .in0(registers_1_read_data_2), .in1(SignExtend), .out(multiplexer_2_out), .sel(ALUSrc));
  ALUControl alucontrol_1 (.ALUOp(ALUOp), .Instruction(Address_Memory_out_2[5:0]), .Select(alucontrol_1_select));
  ALU alu_1 (
    .X(registers_1_read_data_1), .Y(multiplexer_2_out), .ALUSelect(alucontrol_1_select), .O(alu_1_o),
    .Zero(alu_1_zero));
  Shifter #(.width(32)) shifter_1 (.in(SignExtend), .\dist (5'b00010), .out(shifter_1_out));
  Adder #(.width(32)) adder_2 (.a(adder_1_out), .b(shifter_1_out), .out(adder_2_out));  // open: cin, cout
  Data_Memory Data_Memory (
    .Memory_Address(alu_1_o), .Data(registers_1_read_data_2), .MemWrite(MemWrite), .CLK(CLK),
    .Readed_Data(Data_Memory_readed_data));
  Multiplexer #(.width(32), .enable("false")) multiplexer_3 (
    .in0(adder_1_out), .in1(adder_2_out), .out(multiplexer_3_out), .sel(and_1_out));
  and and_1 (and_1_out, Branch, alu_1_zero);
  not not_1 (not_1_out, MemToReg);
  Multiplexer #(.width(32), .enable("false")) multiplexer_4 (
    .in0(Data_Memory_readed_data), .in1(alu_1_o), .out(WriteData), .sel(not_1_out));
endmodule

module PC (
  input  [31:0] Address_Input,
  input  CLK,
  output [31:0] Next_Address
);

  wire not_1_out;

  Counter #(.width(32), .max('hffffffff)) counter_1 (
    .load(1'b1), .D(Address_Input), .count(1'b0), .Q(Next_Address), .clk(not_1_out));  // open: carry, clr
  not not_1 (not_1_out, CLK);
endmodule

// AM
module Address_Memory (
  input  [31:0] Instruction_Address,
  output [31:0] out_2
);

  wire [31:0] shifter_1_out;

  Shifter #(.width(32), .shift("lr")) shifter_1 (.in(Instruction_Address), .\dist (5'b00010), .out(shifter_1_out));
  ROM #(.addrWidth(24), .dataWidth(32)) rom_1 (.addr(shifter_1_out[23:0]), .data(out_2), .sel(1'b1));

  // Notes on the sheet:
  //   contents of rom_1 (hex, n*v repeats v):
  //   20082000 2009201c 8d2a0000 2001d8f1 102a0010 21290004 200c0001 8d0a0000 8d2b0000 2001d8f1 102a000a
  //   2001d8f1 102b0008 20010001 142c0001 ad0b0000 21080004 21290004 2001ffff 71816002 1000fff2 2402000a c
endmodule

// DM
module Data_Memory (
  input  [31:0] Memory_Address,
  input  [31:0] Data,
  input  MemWrite,
  input  CLK,
  output [31:0] Readed_Data
);

  wire [31:0] shifter_1_out;

  Shifter #(.width(32), .shift("lr")) shifter_1 (.in(Memory_Address), .\dist (5'b00010), .out(shifter_1_out));
  RAM #(.addrWidth(24), .dataWidth(32), .bus("separate")) ram_1 (
    .addr(shifter_1_out[23:0]), .din(Data), .data(Readed_Data), .str(MemWrite), .sel(1'b1), .clk(CLK),
    .ld(1'b1), .clr(1'b0));
endmodule

// Register
module Registers (
  input  Write_Enable,
  input  [4:0] Read_Register_1,
  input  [4:0] Read_Register_2,
  input  [4:0] Write_Register,
  input  [31:0] Write_Data,
  input  CLK,
  output [31:0] Read_Data_1,
  output [31:0] Read_data_2
);

  wire and_1_out, and_2_out, and_3_out, and_4_out, and_5_out, and_6_out, and_7_out, and_8_out, and_9_out,
       and_10_out, and_11_out, and_12_out, and_13_out, and_14_out, and_15_out, and_16_out, and_17_out,
       and_18_out, and_19_out, and_20_out, and_21_out, and_22_out, and_23_out, and_24_out, and_25_out,
       and_26_out, and_27_out, and_28_out, and_29_out, and_30_out, and_31_out, and_32_out, decoder_1_out0,
       decoder_1_out1, decoder_1_out2, decoder_1_out3, decoder_1_out4, decoder_1_out5, decoder_1_out6,
       decoder_1_out7, decoder_1_out8, decoder_1_out9, decoder_1_out10, decoder_1_out11, decoder_1_out12,
       decoder_1_out13, decoder_1_out14, decoder_1_out15, decoder_1_out16, decoder_1_out17, decoder_1_out18,
       decoder_1_out19, decoder_1_out20, decoder_1_out21, decoder_1_out22, decoder_1_out23, decoder_1_out24,
       decoder_1_out25, decoder_1_out26, decoder_1_out27, decoder_1_out28, decoder_1_out29, decoder_1_out30,
       decoder_1_out31;
  wire [31:0] register_1_q, register_2_q, register_3_q, register_4_q, register_5_q, register_6_q,
       register_7_q, register_8_q, register_9_q, register_10_q, register_11_q, register_12_q, register_13_q,
       register_14_q, register_15_q, register_16_q, register_17_q, register_18_q, register_19_q,
       register_20_q, register_21_q, register_22_q, register_23_q, register_24_q, register_25_q,
       register_26_q, register_27_q, register_28_q, register_29_q, register_30_q, register_31_q,
       register_32_q;

  Decoder #(.select(5), .enable("false")) decoder_1 (
    .out0(decoder_1_out0), .out1(decoder_1_out1), .out2(decoder_1_out2), .out3(decoder_1_out3),
    .out4(decoder_1_out4), .out5(decoder_1_out5), .out6(decoder_1_out6), .out7(decoder_1_out7),
    .out8(decoder_1_out8), .out9(decoder_1_out9), .out10(decoder_1_out10), .out11(decoder_1_out11),
    .out12(decoder_1_out12), .out13(decoder_1_out13), .out14(decoder_1_out14), .out15(decoder_1_out15),
    .out16(decoder_1_out16), .out17(decoder_1_out17), .out18(decoder_1_out18), .out19(decoder_1_out19),
    .out20(decoder_1_out20), .out21(decoder_1_out21), .out22(decoder_1_out22), .out23(decoder_1_out23),
    .out24(decoder_1_out24), .out25(decoder_1_out25), .out26(decoder_1_out26), .out27(decoder_1_out27),
    .out28(decoder_1_out28), .out29(decoder_1_out29), .out30(decoder_1_out30), .out31(decoder_1_out31),
    .sel(Write_Register));
  Register #(.width(32)) register_1 (.D(Write_Data), .en(and_1_out), .Q(register_1_q), .clk(CLK));  // open: clr
  and and_1 (and_1_out, decoder_1_out0, Write_Enable);
  Register #(.width(32)) register_2 (.D(Write_Data), .en(and_2_out), .Q(register_2_q), .clk(CLK));  // open: clr
  and and_2 (and_2_out, decoder_1_out1, Write_Enable);
  Register #(.width(32)) register_3 (.D(Write_Data), .en(and_3_out), .Q(register_3_q), .clk(CLK));  // open: clr
  and and_3 (and_3_out, decoder_1_out2, Write_Enable);
  Register #(.width(32)) register_4 (.D(Write_Data), .en(and_4_out), .Q(register_4_q), .clk(CLK));  // open: clr
  and and_4 (and_4_out, decoder_1_out3, Write_Enable);
  Register #(.width(32)) register_5 (.D(Write_Data), .en(and_5_out), .Q(register_5_q), .clk(CLK));  // open: clr
  and and_5 (and_5_out, decoder_1_out4, Write_Enable);
  Register #(.width(32)) register_6 (.D(Write_Data), .en(and_6_out), .Q(register_6_q), .clk(CLK));  // open: clr
  and and_6 (and_6_out, decoder_1_out5, Write_Enable);
  Register #(.width(32)) register_7 (.D(Write_Data), .en(and_7_out), .Q(register_7_q), .clk(CLK));  // open: clr
  and and_7 (and_7_out, decoder_1_out6, Write_Enable);
  Register #(.width(32)) register_8 (.D(Write_Data), .en(and_8_out), .Q(register_8_q), .clk(CLK));  // open: clr
  and and_8 (and_8_out, decoder_1_out7, Write_Enable);
  Register #(.width(32)) register_9 (.D(Write_Data), .en(and_9_out), .Q(register_9_q), .clk(CLK));  // open: clr
  and and_9 (and_9_out, decoder_1_out8, Write_Enable);
  Register #(.width(32)) register_10 (.D(Write_Data), .en(and_10_out), .Q(register_10_q), .clk(CLK));  // open: clr
  and and_10 (and_10_out, decoder_1_out9, Write_Enable);
  Register #(.width(32)) register_11 (.D(Write_Data), .en(and_11_out), .Q(register_11_q), .clk(CLK));  // open: clr
  and and_11 (and_11_out, decoder_1_out10, Write_Enable);
  Register #(.width(32)) register_12 (.D(Write_Data), .en(and_12_out), .Q(register_12_q), .clk(CLK));  // open: clr
  and and_12 (and_12_out, decoder_1_out11, Write_Enable);
  Register #(.width(32)) register_13 (.D(Write_Data), .en(and_13_out), .Q(register_13_q), .clk(CLK));  // open: clr
  and and_13 (and_13_out, decoder_1_out12, Write_Enable);
  Register #(.width(32)) register_14 (.D(Write_Data), .en(and_14_out), .Q(register_14_q), .clk(CLK));  // open: clr
  and and_14 (and_14_out, decoder_1_out13, Write_Enable);
  Register #(.width(32)) register_15 (.D(Write_Data), .en(and_15_out), .Q(register_15_q), .clk(CLK));  // open: clr
  and and_15 (and_15_out, decoder_1_out14, Write_Enable);
  Register #(.width(32)) register_16 (.D(Write_Data), .en(and_16_out), .Q(register_16_q), .clk(CLK));  // open: clr
  and and_16 (and_16_out, decoder_1_out15, Write_Enable);
  Register #(.width(32)) register_17 (.D(Write_Data), .en(and_17_out), .Q(register_17_q), .clk(CLK));  // open: clr
  and and_17 (and_17_out, decoder_1_out16, Write_Enable);
  Register #(.width(32)) register_18 (.D(Write_Data), .en(and_18_out), .Q(register_18_q), .clk(CLK));  // open: clr
  and and_18 (and_18_out, decoder_1_out17, Write_Enable);
  Register #(.width(32)) register_19 (.D(Write_Data), .en(and_19_out), .Q(register_19_q), .clk(CLK));  // open: clr
  and and_19 (and_19_out, decoder_1_out18, Write_Enable);
  Register #(.width(32)) register_20 (.D(Write_Data), .en(and_20_out), .Q(register_20_q), .clk(CLK));  // open: clr
  and and_20 (and_20_out, decoder_1_out19, Write_Enable);
  Register #(.width(32)) register_21 (.D(Write_Data), .en(and_21_out), .Q(register_21_q), .clk(CLK));  // open: clr
  and and_21 (and_21_out, decoder_1_out20, Write_Enable);
  Register #(.width(32)) register_22 (.D(Write_Data), .en(and_22_out), .Q(register_22_q), .clk(CLK));  // open: clr
  and and_22 (and_22_out, decoder_1_out21, Write_Enable);
  Register #(.width(32)) register_23 (.D(Write_Data), .en(and_23_out), .Q(register_23_q), .clk(CLK));  // open: clr
  and and_23 (and_23_out, decoder_1_out22, Write_Enable);
  Register #(.width(32)) register_24 (.D(Write_Data), .en(and_24_out), .Q(register_24_q), .clk(CLK));  // open: clr
  and and_24 (and_24_out, decoder_1_out23, Write_Enable);
  Register #(.width(32)) register_25 (.D(Write_Data), .en(and_25_out), .Q(register_25_q), .clk(CLK));  // open: clr
  and and_25 (and_25_out, decoder_1_out24, Write_Enable);
  Register #(.width(32)) register_26 (.D(Write_Data), .en(and_26_out), .Q(register_26_q), .clk(CLK));  // open: clr
  and and_26 (and_26_out, decoder_1_out25, Write_Enable);
  Register #(.width(32)) register_27 (.D(Write_Data), .en(and_27_out), .Q(register_27_q), .clk(CLK));  // open: clr
  and and_27 (and_27_out, decoder_1_out26, Write_Enable);
  Register #(.width(32)) register_28 (.D(Write_Data), .en(and_28_out), .Q(register_28_q), .clk(CLK));  // open: clr
  and and_28 (and_28_out, decoder_1_out27, Write_Enable);
  Register #(.width(32)) register_29 (.D(Write_Data), .en(and_29_out), .Q(register_29_q), .clk(CLK));  // open: clr
  and and_29 (and_29_out, decoder_1_out28, Write_Enable);
  Register #(.width(32)) register_30 (.D(Write_Data), .en(and_30_out), .Q(register_30_q), .clk(CLK));  // open: clr
  and and_30 (and_30_out, decoder_1_out29, Write_Enable);
  Register #(.width(32)) register_31 (.D(Write_Data), .en(and_31_out), .Q(register_31_q), .clk(CLK));  // open: clr
  and and_31 (and_31_out, decoder_1_out30, Write_Enable);
  Register #(.width(32)) register_32 (.D(Write_Data), .en(and_32_out), .Q(register_32_q), .clk(CLK));  // open: clr
  and and_32 (and_32_out, decoder_1_out31, Write_Enable);
  Multiplexer #(.select(5), .width(32), .enable("false")) multiplexer_1 (
    .in0(register_1_q), .in1(register_2_q), .in2(register_3_q), .in3(register_4_q), .in4(register_5_q),
    .in5(register_6_q), .in6(register_7_q), .in7(register_8_q), .in8(register_9_q), .in9(register_10_q),
    .in10(register_11_q), .in11(register_12_q), .in12(register_13_q), .in13(register_14_q),
    .in14(register_15_q), .in15(register_16_q), .in16(register_17_q), .in17(register_18_q),
    .in18(register_19_q), .in19(register_20_q), .in20(register_21_q), .in21(register_22_q),
    .in22(register_23_q), .in23(register_24_q), .in24(register_25_q), .in25(register_26_q),
    .in26(register_27_q), .in27(register_28_q), .in28(register_29_q), .in29(register_30_q),
    .in30(register_31_q), .in31(register_32_q), .out(Read_Data_1), .sel(Read_Register_1));
  Multiplexer #(.select(5), .width(32), .enable("false")) multiplexer_2 (
    .in0(register_1_q), .in1(register_2_q), .in2(register_3_q), .in3(register_4_q), .in4(register_5_q),
    .in5(register_6_q), .in6(register_7_q), .in7(register_8_q), .in8(register_9_q), .in9(register_10_q),
    .in10(register_11_q), .in11(register_12_q), .in12(register_13_q), .in13(register_14_q),
    .in14(register_15_q), .in15(register_16_q), .in16(register_17_q), .in17(register_18_q),
    .in18(register_19_q), .in19(register_20_q), .in20(register_21_q), .in21(register_22_q),
    .in22(register_23_q), .in23(register_24_q), .in24(register_25_q), .in25(register_26_q),
    .in26(register_27_q), .in27(register_28_q), .in28(register_29_q), .in29(register_30_q),
    .in30(register_31_q), .in31(register_32_q), .out(Read_data_2), .sel(Read_Register_2));

  // Other names for the same wires on the sheet: WE = Write_Enable
endmodule

module Control (
  input  [5:0] Instruction,
  output RegDst,
  output Branch,
  output MemToReg,
  output [1:0] ALUOp,
  output MemWrite,
  output ALUSrc,
  output RegWrite
);

  ROM #(.addrWidth(6)) rom_1 (
    .addr(Instruction), .data({RegDst, Branch, MemToReg, ALUOp, MemWrite, ALUSrc, RegWrite}), .sel(1'b1));

  // Notes on the sheet:
  //   contents of rom_1 (hex, n*v repeats v):
  //   99 0 0 0 40 48 0 0 13 19*0 99 6*0 33 7*0 16
endmodule

module ALU (
  input  [31:0] X,
  input  [31:0] Y,
  input  [2:0] ALUSelect,
  output [31:0] O,
  output Zero
);

  wire and_1_out, comparator_1_lt, not_1_out, Zero_t;
  wire [31:0] adder_1_out, and_2_out, bit_extender_1_out, multiplier_1_out, nor_1_out, or_1_out,
       subtractor_1_out;

  Multiplexer #(.enable("false")) multiplexer_1 (.in0(Zero_t), .in1(not_1_out), .out(Zero), .sel(and_1_out));
  not not_1 (not_1_out, Zero_t);
  and and_1 (and_1_out, ALUSelect[2], ~ALUSelect[1], ALUSelect[0]);  // AND_Gate
  assign nor_1_out = ~(X | Y);  // NOR_Gate nor_1, 32 bits wide
  Adder #(.width(32)) adder_1 (.a(X), .b(Y), .out(adder_1_out));  // open: cin, cout
  Subtractor #(.width(32)) subtractor_1 (.a(X), .b(Y), .out(subtractor_1_out));  // open: bin, bout
  Comparator #(.width(32)) comparator_1 (.a(X), .b(Y), .eq(Zero_t), .lt(comparator_1_lt));  // open: gt
  Multiplier #(.width(32)) multiplier_1 (.a(X), .b(Y), .out(multiplier_1_out));  // open: cin, cout
  assign and_2_out = X & Y;  // AND_Gate and_2, 32 bits wide
  assign or_1_out = X | Y;  // OR_Gate or_1, 32 bits wide
  assign bit_extender_1_out = {{31{1'b0}}, comparator_1_lt};  // Bit_Extender bit_extender_1
  Multiplexer #(.select(3), .width(32), .enable("false")) multiplexer_2 (
    .in0(nor_1_out), .in1(adder_1_out), .in2(subtractor_1_out), .in3(bit_extender_1_out),
    .in4(multiplier_1_out), .in5({32{1'b0}}), .in6(and_2_out), .in7(or_1_out), .out(O), .sel(ALUSelect));

  // Other names for the same wires on the sheet: OUT[31:0] = O; Select[2:0] = ALUSelect
endmodule

module ALUControl (
  input  [1:0] ALUOp,
  input  [5:0] Instruction,
  output [2:0] Select
);

  wire [2:0] Select_t;

  // Probe on Instruction
  ROM #(.addrWidth(6), .dataWidth(3)) rom_1 (.addr(Instruction), .data(Select_t), .sel(1'b1));
  Multiplexer #(.select(2), .width(3), .enable("false")) multiplexer_1 (
    .in0(3'b011), .in1(3'b101), .in2(3'b001), .in3(Select_t), .out(Select), .sel(ALUOp));

  // Other names for the same wires on the sheet: Instr[5:0] = Instruction

  // Notes on the sheet:
  //   contents of rom_1 (hex, n*v repeats v):
  //   0 0 4 5*0 1 15*0 4 7*0 1 0 2 0 7 6 4*0 3
endmodule
